# Fritzing sketch ModuloPrincipal (saved by Fritzing 0.8.7b)
circuit board: 10.5689cm x 9.60011cm
breadboards: 1

parts:
  P8 = 46 Pins Beagle [form="♂ (male)" package=THT]  # not connected
  P9 = 46 Pins Beagle [form="♂ (male)" package=THT]
  U1 = Voltage Regulator - 5V [package="TO220 [THT]"]
  C1 = Electrolytic Capacitor [capacitance=220µF voltage=16V package="100 mil [THT, electrolytic]"]
  C2 = Electrolytic Capacitor [capacitance=33µF package="100 mil [THT, electrolytic]"]
  C3 = Ceramic Capacitor [capacitance=0.1µF package="100 mil [THT, multilayer]"]
  C4 = Ceramic Capacitor [capacitance=0.1µF package="100 mil [THT, multilayer]"]
  J1 = female pin header, 2 pins [form="♀ (female)"]
  D1 = Diode [package=diode-1n4001]
  CD4051B = IC, DIP package, 16 pins [chip_label=CD4051B]
  J3 = female pin header, 16 pins [form="♀ (female)"]

nets:
  3.3V: P9.pin4, CD4051B.pin16
  5V: P9.pin5, U1.output_voltage, C2.+, C4.1
  N1: P9.pin27, CD4051B.pin11
  N2: P9.pin30, CD4051B.pin10
  N3: P9.pin32, J3.pin15
  N4: P9.pin33, J3.pin5
  N5: P9.pin34, J3.pin16
  N6: P9.pin35, CD4051B.pin3
  N7: P9.pin36, J3.pin6
  N8: P9.pin37, J3.pin3
  N9: P9.pin38, J3.pin4
  N10: P9.pin39, J3.pin1
  N11: P9.pin40, J3.pin2
  N12: P9.pin42, CD4051B.pin9
  GND: P9.pin46, U1.GND, C1.-, C2.-, C3.0, C4.0, J1.pin2, CD4051B.pin6, CD4051B.pin7, CD4051B.pin8
  N13: U1.input_voltage, C1.+, C3.1, D1.C
  N14: J1.pin1, D1.A
  N15: CD4051B.pin1, J3.pin11
  N16: CD4051B.pin2, J3.pin13
  N17: CD4051B.pin4, J3.pin14
  N18: CD4051B.pin5, J3.pin12
  N19: CD4051B.pin12, J3.pin10
  N20: CD4051B.pin13, J3.pin7
  N21: CD4051B.pin14, J3.pin8
  N22: CD4051B.pin15, J3.pin9

custom parts:
  46 Pins Beagle: 46 pins beagle
